# Fritzing sketch Araba (saved by Fritzing 0.9.3b)
breadboards: 1

parts:
  Parça1 = Arduino Uno (Rev3)
  LED1 = LED - 5mm [color="Red (633nm)" package="5 mm [THT]"]
  M1 = DC Motor
  M2 = DC Motor
  U2 = BATTERY-2 [package=battery-aaa]
  U3 = BATTERY-2 [package=battery-aaa]
  U4 = BATTERY-2 [package=battery-aaa]
  U5 = BATTERY-2 [package=battery-aaa]
  U6 = BATTERY-2 [package=battery-aaa]
  R1 = Photocell (LDR) [package=THT]
  hc-sr1 = hc-sr04
  Parça2 = Bluetooth HC-05 Macho
  IC1 = L293D [package=THT]
  SG1 = Buzzer 12mm [package=buzzer-ccv-kit]
  R2 = Resistor [tolerance=±5% resistance=220 package=THT]
  Parça3 = MicroSD Card Module
  R3 = Resistor [tolerance=±5% resistance=220 package=THT]

nets:
  N1: Parça1.A0, R1.pin_1
  N2: Parça1.A1, IC1.In_1
  N3: Parça1.A2, IC1.In_2
  N4: Parça1.A3, IC1.In_4
  N5: Parça1.A4/SDA, IC1.In_3
  N6: Parça1.D8, SG1.1
  N7: Parça1.D11_PWM/MOSI, Parça3.MOSI
  N8: Parça1.D12/MISO, Parça3.MISO
  N9: Parça1.D13/SCK, Parça3.SCK
  GND: Parça1.GND, U5.+1, hc-sr1.GND, IC1.0V, R2.Pin_0, Parça3.GND, R3.Pin_1
  N10: Parça1.D2, Parça2.TXD
  N11: Parça1.D3_PWM, Parça2.RXD
  N12: Parça1.D4, Parça3.CS
  N13: Parça1.D5_PWM, LED1.anode
  N14: Parça1.D6_PWM, hc-sr1.Echo
  N15: Parça1.D7, hc-sr1.Trig
  VCC: Parça1.5V, R1.pin_0, hc-sr1.VCC, Parça2.VCC, IC1.Enable_1, IC1.+V, Parça3.VCC
  N16: LED1.cathode, R2.Pin_1
  N17: M1.pin_1, IC1.Out_4_(_Controlled_by_Enable_2_)
  N18: M1.pin_2, IC1.Out_3_(_Controlled_by_Enable_2_)
  N19: M2.pin_1, IC1.Out_2_(_Controlled_by_Enable_1_)
  N20: M2.pin_2, IC1.Out_1_(_Controlled_by_Enable_1_)
  N21: U2.-1, U6.+1
  N22: U2.+1, U3.-1
  N23: U3.+1, U4.-1
  N24: U4.+1, U5.-1
  N25: U6.-1, IC1.+Vmotor
  N26: SG1.2, R3.Pin_0
